// Logisim project alu.circ as structural Verilog: 15 circuits, main circuit main
module main (
  input  [31:0] X,
  input  [31:0] Y,
  input  [3:0] Switch,
  output Signed_Overflow,
  output Equal,
  output [31:0] Result
);

  wire overflowAdd, overflowSub;
  wire [31:0] add, addu, \and , \or , sll, slt, sltu, sra, srl, sub, subu, \xor ;

  add add_1 (.X(X), .Y(Y), .overFlow(overflowAdd), .out(add));
  addu addu_1 (.X(X), .Y(Y), .out(addu));
  Comparator #(.width(32)) comparator_1 (.a(X), .b(Y), .eq(Equal));  // open: gt, lt
  sub sub_1 (.X(X), .Y(Y), .overFlow(overflowSub), .out(sub));
  subu subu_1 (.X(X), .Y(Y), .out(subu));
  \and  and_1 (.X(X), .Y(Y), .out(\and ));
  Multiplexer #(.select(4), .width(32)) multiplexer_1 (
    .in0(add), .in1(addu), .in2(sub), .in3(subu), .in4(\and ), .in5(\or ), .in6(\xor ), .in7(slt),
    .in8(sltu), .in9(sll), .in10(srl), .in11(sra), .out(Result), .sel(Switch));  // open: in12, in13, in14, in15, en
  Multiplexer #(.select(4)) multiplexer_2 (
    .in0(overflowAdd), .in1(1'b0), .in2(overflowSub), .in3(1'b0), .in4(1'b0), .in5(1'b0), .in6(1'b0),
    .in7(1'b0), .in8(1'b0), .in9(1'b0), .in10(1'b0), .in11(1'b0), .in12(1'b0), .in13(1'b0), .in14(1'b0),
    .in15(1'b0), .out(Signed_Overflow), .sel(Switch));  // open: en
  \or  or_1 (.X(X), .Y(Y), .out(\or ));
  \xor  xor_1 (.X(X), .Y(Y), .out(\xor ));
  sll sll_1 (.Y(Y), .X(X), .out(sll));
  srl srl_1 (.Y(Y), .X(X), .out(srl));
  sra sra_1 (.Y(Y), .X(X), .out(sra));
  slt slt_1 (.X(X), .Y(Y), .out(slt));
  sltu sltu_1 (.X(X), .Y(Y), .out(sltu));

  // Other names for the same wires on the sheet: overflow = Signed_Overflow; S[3:0] = Switch

  // Notes on the sheet:
  //   INPUTS to your circuit
  //   add
  //   addu
  //   equal
  //   sub
  //   subu
  //   and
  //   DON'T CHANGE THE LOCATIONS OF THE INPUTS AND OUTPUTS!
  //   or
  //   xor
  //   sll
  //   srl
  //   sra
  //   slt
  //   sltu
  //   MUX for each subcircuit
  //   MUX for overflow 
  //   OUTPUTS from your circuit
endmodule

module add (
  input  [31:0] X,
  input  [31:0] Y,
  output overFlow,
  output [31:0] out
);

  addOF addof_1 (.X(X), .Y(Y), .Sum(out), .overflow(overFlow));
  Adder #(.width(32)) adder_1 (.a(X), .b(Y), .out(out), .cin(1'b0));  // open: cout

  // Notes on the sheet:
  //   subcircuit for overflow
endmodule

module addu (
  input  [31:0] X,
  input  [31:0] Y,
  output [31:0] out
);

  Adder #(.width(32)) adder_1 (.a(X), .b(Y), .out(out), .cin(1'b0));  // open: cout

  // Notes on the sheet:
  //   simple adder
endmodule

module sub (
  input  [31:0] X,
  input  [31:0] Y,
  output overFlow,
  output [31:0] out
);

  subOF subof_1 (.X(X), .Y(Y), .Sum(out), .out(overFlow));
  Subtractor #(.width(32)) subtractor_1 (.a(X), .b(Y), .out(out), .bin(1'b0));  // open: bout

  // Notes on the sheet:
  //   subcircuit for overflow
endmodule

module subu (
  input  [31:0] X,
  input  [31:0] Y,
  output [31:0] out
);

  Subtractor #(.width(32)) subtractor_1 (.a(X), .b(Y), .out(out), .bin(1'b0));  // open: bout

  // Notes on the sheet:
  //   simple subtract
endmodule

module \and  (
  input  [31:0] X,
  input  [31:0] Y,
  output [31:0] out
);

  assign out = X & Y;  // AND_Gate and_1, 32 bits wide

  // Notes on the sheet:
  //   and gate
endmodule

module \or  (
  input  [31:0] X,
  input  [31:0] Y,
  output [31:0] out
);

  assign out = X | Y;  // OR_Gate or_1, 32 bits wide

  // Notes on the sheet:
  //   or gate
endmodule

module \xor  (
  input  [31:0] X,
  input  [31:0] Y,
  output [31:0] out
);

  assign out = X ^ Y;  // XOR_Gate xor_1, 32 bits wide

  // Notes on the sheet:
  //   xor gate
endmodule

module slt (
  input  [31:0] X,
  input  [31:0] Y,
  output [31:0] out
);

  wire comparator_1_lt;

  Comparator #(.width(32)) comparator_1 (.a(X), .b(Y), .lt(comparator_1_lt));  // open: gt, eq
  assign out = {{31{1'b0}}, comparator_1_lt};  // Bit_Extender bit_extender_1

  // Notes on the sheet:
  //   Need to extend 1 bit to 32 bit to work properly
endmodule

module sltu (
  input  [31:0] X,
  input  [31:0] Y,
  output [31:0] out
);

  wire comparator_1_lt;

  Comparator #(.width(32), .mode("unsigned")) comparator_1 (.a(X), .b(Y), .lt(comparator_1_lt));  // open: gt, eq
  assign out = {{31{1'b0}}, comparator_1_lt};  // Bit_Extender bit_extender_1

  // Notes on the sheet:
  //   Ned to extend 1 bit comparator to 32 bit
endmodule

module sll (
  input  [31:0] Y,
  input  [31:0] X,
  output [31:0] out
);

  Shifter #(.width(32)) shifter_1 (.in(Y), .\dist (X[4:0]), .out(out));

  // Notes on the sheet:
  //   Use splitter to get 5 least significant bits for shift
endmodule

module srl (
  input  [31:0] Y,
  input  [31:0] X,
  output [31:0] out
);

  Shifter #(.width(32), .shift("lr")) shifter_1 (.in(Y), .\dist (X[4:0]), .out(out));

  // Notes on the sheet:
  //   Use splitter to get 5 least significant bits for shift
endmodule

module sra (
  input  [31:0] Y,
  input  [31:0] X,
  output [31:0] out
);

  Shifter #(.width(32), .shift("ar")) shifter_1 (.in(Y), .\dist (X[4:0]), .out(out));

  // Notes on the sheet:
  //   Use splitter to get 5 least significant bits for shift
endmodule

module addOF (
  input  [31:0] X,
  input  [31:0] Y,
  input  [31:0] Sum,
  output overflow
);

  wire and_1_out, and_2_out, and_3_out, and_4_out, not_1_out, not_2_out, not_3_out;

  and and_1 (and_1_out, X[31], Y[31]);
  not not_1 (not_1_out, Sum[31]);
  not not_2 (not_2_out, X[31]);
  not not_3 (not_3_out, Y[31]);
  and and_2 (and_2_out, not_2_out, not_3_out);
  and and_3 (and_3_out, and_1_out, not_1_out);
  and and_4 (and_4_out, Sum[31], and_2_out);
  or or_1 (overflow, and_3_out, and_4_out);

  // Other names for the same wires on the sheet: result = Sum[31]; X_t = X[31]; Y_t = Y[31]

  // Notes on the sheet:
  //   OverFlow Logic
  //   Comparing the 31st bit of each input to the sum in order to detect overflow
  //   If numbers add have same sign overflow occurs if the result has opposite sign
endmodule

module subOF (
  input  [31:0] X,
  input  [31:0] Y,
  input  [31:0] Sum,
  output out
);

  wire and_1_out, and_2_out, and_3_out, comparator_1_eq, not_1_out, not_2_out, not_3_out, not_4_out,
       not_5_out, not_6_out, or_1_out, or_2_out;

  not not_1 (not_1_out, X[31]);
  not not_2 (not_2_out, Sum[31]);
  not not_3 (not_3_out, Y[31]);
  not not_4 (not_4_out, comparator_1_eq);
  not not_5 (not_5_out, Sum[31]);
  not not_6 (not_6_out, Y[31]);
  and and_1 (and_1_out, not_1_out, Sum[31], Y[31]);
  and and_2 (and_2_out, X[31], not_2_out, not_3_out);
  and and_3 (and_3_out, not_4_out, not_5_out, not_6_out);
  Comparator #(.width(32)) comparator_1 (.a(Sum), .b({32{1'b0}}), .eq(comparator_1_eq));  // open: gt, lt
  or or_1 (or_1_out, and_1_out, and_2_out);
  or or_2 (or_2_out, or_1_out, and_3_out);
  not not_7 (out, or_2_out);

  // Other names for the same wires on the sheet: result = Sum[31]; X_t = X[31]; Y_t = Y[31]

  // Notes on the sheet:
  //   OverFlow Logic
  //   Check if 0
  //   Comparing the 31st bit of each input to the sum in order to detect overflow
  //   Overflow occurs if the result has same sign as subtractor
endmodule
